# Fritzing sketch musclefuel_dispenser_schematic (saved by Fritzing 0.9.4)
breadboards: 2

parts:
  Raspberry_Pi_1 = Raspberry Pi 3 [part_number=RPI-3-V1.2]
  HC-SR04_Sensor_1 = HC-SR04 Ultrasonic Distance Sensor
  HC-SR04_Sensor_2 = HC-SR04 Ultrasonic Distance Sensor
  Part1 = HX711 Weighing Sensor Module
  LCD1 = LCD screen
  U3 = PCF8574 [package="DIP16 [THT]"]
  S1 = SWITCH-MOMENTARY-2 [package=tactile_switch_tall]
  R2 = Resistor [tolerance=±5% resistance=1k package=THT]
  J2 = LOAD_CELL [package=1x03]
  Part2 = HX711 Weighing Sensor Module
  J3 = LOAD_CELL [package=1x03]
  RE1 = KY-040 Rotary encoder [package=THT]
  U4 = POT [package=pot_alpha_rv16af-20]
  BB_PWR1 = Toaster Bread Board Dual Supply [package="DIP (Dual Inline) [THT]"]
  Driver3 = 28BYJ-48 Driver Module [part_number=ULN2003 package=THT]
  SM3 = 28BYJ-48 Stepper Motor [part_number=28BYJ-48]
  Driver4 = 28BYJ-48 Driver Module [part_number=ULN2003 package=THT]
  SM4 = 28BYJ-48 Stepper Motor [part_number=28BYJ-48]
  R3 = Resistor [tolerance=±5% resistance=470 package="1206 [SMD]"]
  R4 = Resistor [tolerance=±5% resistance=1k package="1206 [SMD]"]
  R5 = Resistor [tolerance=±5% resistance=470 package="1206 [SMD]"]
  R6 = Resistor [tolerance=±5% resistance=1k package="1206 [SMD]"]
  WATER_PUMP1 = water pump/motor
  R7 = Resistor [tolerance=±5% resistance=1k package="0402 [SMD]"]
  Q2 = NPN-Transistor [package="TO92 [THT]"]

nets (from the schematic view):
  N1: Raspberry_Pi_1.GPIO2, U3.SDA
  N2: Raspberry_Pi_1.GPIO3, U3.SCL
  N3: Raspberry_Pi_1.GPIO4, R2.Pin_1
  N4: Raspberry_Pi_1.GPIO17, Driver3.IN1
  N5: Raspberry_Pi_1.GPIO27, Driver3.IN2
  N6: Raspberry_Pi_1.GPIO22, Driver3.IN3
  N7: Raspberry_Pi_1.GPIO10, R5.Pin_1, R6.Pin_0
  N8: Raspberry_Pi_1.GPIO9, HC-SR04_Sensor_2.TRIG
  N9: Raspberry_Pi_1.GPIO11, R3.Pin_1, R4.Pin_0
  GND: Raspberry_Pi_1.GND, HC-SR04_Sensor_1.ECHO, HC-SR04_Sensor_2.ECHO, Part1.GND, LCD1.VSS, LCD1.R/W, LCD1.LED-, U3.A0, U3.A1, U3.A2, U3.GND, S1.2, S1.1, R2.Pin_0, Part2.GND, RE1.GND, U4.A, BB_PWR1.GND, Driver3.GND, Driver4.GND, R4.Pin_1, R6.Pin_1, WATER_PUMP1.pin_2
  N10: Raspberry_Pi_1.GPIO5, Driver3.IN4
  N11: Raspberry_Pi_1.GPIO6, Driver4.IN1
  N12: Raspberry_Pi_1.GPIO13, Driver4.IN2
  N13: Raspberry_Pi_1.GPIO19, Driver4.IN3
  N14: Raspberry_Pi_1.GPIO26, Driver4.IN4
  N15: Raspberry_Pi_1.GPIO21, LCD1.RS
  N16: Raspberry_Pi_1.GPIO20, LCD1.E
  N17: Raspberry_Pi_1.GPIO16, R7.Pin_0
  N18: Raspberry_Pi_1.GPIO12, HC-SR04_Sensor_1.TRIG
  N19: Raspberry_Pi_1.GPIO7, Part1.DO/RX
  N20: Raspberry_Pi_1.GPIO8, Part1.CK/TX
  N21: Raspberry_Pi_1.GPIO25, RE1.CLK
  N22: Raspberry_Pi_1.GPIO24, RE1.DT
  N23: Raspberry_Pi_1.GPIO23, RE1.SW
  N24: Raspberry_Pi_1.GPIO18, Part2.DO/RX
  N25: Raspberry_Pi_1.GPIO15, Part2.CK/TX
  VCC: HC-SR04_Sensor_1.VCC, HC-SR04_Sensor_2.VCC, U3.VCC, RE1.Vcc, BB_PWR1.VS2
  N26: HC-SR04_Sensor_1.GND, R3.Pin_0
  N27: HC-SR04_Sensor_2.GND, R5.Pin_0
  VCC_2: Part1.VCC, LCD1.VDD, LCD1.LED+, Part2.VCC, U4.E, BB_PWR1.VS1, Driver3.Vmotor, Driver4.Vmotor, Q2.C
  N28: Part1.E+, J2.W
  N29: Part1.E-, J2.B
  N30: Part1.A-, J2.R
  N31: LCD1.V0, U4.S
  N32: LCD1.DB0, U3.P0
  N33: LCD1.DB1, U3.P1
  N34: LCD1.DB2, U3.P2
  N35: LCD1.DB3, U3.P3
  N36: LCD1.DB4, U3.P4
  N37: LCD1.DB5, U3.P5
  N38: LCD1.DB6, U3.P6
  N39: LCD1.DB7, U3.P7
  N40: Part2.E+, J3.W
  N41: Part2.E-, J3.B
  N42: Part2.A-, J3.R
  N43: Driver3.blue-pin, SM3.blue-pin
  N44: Driver3.pink-pin, SM3.pink-pin
  N45: Driver3.yellow-pin, SM3.yellow-pin
  N46: Driver3.orange-pin, SM3.orange-pin
  N47: Driver3.red-pin, SM3.red-pin
  N48: Driver4.blue-pin, SM4.blue-pin
  N49: Driver4.pink-pin, SM4.pink-pin
  N50: Driver4.yellow-pin, SM4.yellow-pin
  N51: Driver4.orange-pin, SM4.orange-pin
  N52: Driver4.red-pin, SM4.red-pin
  N53: WATER_PUMP1.pin_1, Q2.E
  N54: R7.Pin_1, Q2.B

custom parts:
  KY-040 Rotary encoder: KY-040 Rotary Encoder with switch on breakout borad from AZ Delivery
  Toaster Bread Board Dual Supply: Toaster is dual output USB step up power supply module designed to fit snuggly into a breadboard. It is powered by a single 5V USB port or charger and outputs three voltages simultaneously, these being 3.3V, 5V and a variable supply which is capable of 5V to 16V.
  28BYJ-48 Driver Module: ULN2003 Driver Module for the 28BYJ-48 Unipolar Stepper Motor LED A - Blue wire - Bottom coil left LED B - Pink wire - Top coil left LED C - Yellow wire - Bottom coil right LED D - Orange wire - Top coil right Common rail - red Connector pins: blue - pink - yellow - orange - red Control pins - IN1 to IN4 Power pins - GND & Vmotor (5-12V) On/Off jumper (if removed, power to motor is cut).
  28BYJ-48 Stepper Motor: Unipolar Stepper Motor 28BYJ-48 Top coil - pink & orange Bottom coil - blue & yellow Common rail - red Connector pins: blue - pink - yellow - orange - red
  water pump/motor: WATER PUMP BY ARDUBLOCKTR
